# Fritzing sketch esquema (saved by Fritzing 0.9.6b)

parts:
  Componente2 = Arduino Uno (Rev3) - ICSP
  IC1 = AD8232 HeartRate Monitor [part_number=SEN-12650 chip_label=IC package="DIP (Dual Inline) [THT]"]
  BT2 = Bluetooth HC-06u [package=THT]

nets:
  N1: Componente2.A0, IC1.OUTPUT
  N2: Componente2.ICSP_MOSI, Componente2.D11_PWM/MOSI, IC1.LO-
  N3: Componente2.D10_PWM/SS, IC1.LO+
  GND: Componente2.GND, IC1.GND
  N4: Componente2.D2, BT2.TXD
  N5: Componente2.D3_PWM, BT2.RXD
  3V3: Componente2.3V3, IC1.3.3v
  5V: Componente2.5V, BT2.VCC

custom parts:
  AD8232 HeartRate Monitor: A DIP stand-in part for whatever IC you want. With 10 pins on a 600mil dual inline package (DIP) footprint.
  Bluetooth HC-06u: Bluetooth HC-06 - face up, pins down 16.5mm x 37.5mm PCB
